// Logisim project P115.circ as structural Verilog: 1 circuit, main circuit main
module main (
  input  J,
  input  K,
  input  D,
  input  T,
  output Q,
  output Q_prime,
  output Q_2,
  output Q_prime_2,
  output Q_3,
  output Q_prime_3
);

  wire clock_1_out, clock_2_out, clock_3_out;

  Clock clock_1 (.out(clock_1_out));
  Clock clock_2 (.out(clock_2_out));
  Clock clock_3 (.out(clock_3_out));
  J_K_Flip_Flop j_k_ff_1 (.J(J), .clk(clock_1_out), .K(K), .Q(Q), .Qn(Q_prime));  // open: preset, en, reset
  D_Flip_Flop d_ff_1 (.clk(clock_2_out), .D(D), .Q(Q_2), .Qn(Q_prime_2));  // open: preset, en, reset
  T_Flip_Flop t_ff_1 (.clk(clock_3_out), .T(T), .Q(Q_3), .Qn(Q_prime_3));  // open: preset, reset, en

  // Notes on the sheet:
  //   CLK
  //   CLK
  //   CLK
  //   JK-FLIPFLOP
  //   D-FLIPFLOP
  //   T-FLIPFLOP
endmodule
