// Logisim project p11.circ as structural Verilog: 2 circuits, main circuit main
module main (
  input  in_1,
  input  in_2,
  input  in_3,
  output out_4
);

  wire and_1_out, and_2_out, and_3_out, and_4_out, not_1_out, not_2_out, not_3_out, or_1_out;

  not not_1 (not_1_out, in_1);
  not not_2 (not_2_out, in_2);
  and and_1 (and_1_out, not_1_out, not_2_out);
  not not_3 (not_3_out, in_3);
  and and_2 (and_2_out, and_1_out, in_3);
  and and_3 (and_3_out, in_2, not_3_out);
  or or_1 (or_1_out, and_2_out, and_3_out);
  and and_4 (and_4_out, in_1, in_2);
  or or_2 (out_4, or_1_out, and_4_out);
endmodule

module f_a_b_c (
  input  a,
  input  b,
  input  c,
  output f
);

  wire and_1_out, and_2_out, and_3_out, and_4_out, not_1_out, not_2_out, not_3_out, or_1_out;

  not not_1 (not_1_out, a);
  not not_2 (not_2_out, b);
  and and_1 (and_1_out, not_1_out, not_2_out);
  not not_3 (not_3_out, c);
  and and_2 (and_2_out, and_1_out, c);
  and and_3 (and_3_out, b, not_3_out);
  or or_1 (or_1_out, and_2_out, and_3_out);
  and and_4 (and_4_out, a, b);
  or or_2 (f, or_1_out, and_4_out);
endmodule
